// Logisim project 计算机组成原理-东北大学-实验.circ as structural Verilog
module \实验1_七段数码管显示译码电路  (
);

  wire clock_1_out, \译码电路1_y1 , \译码电路1_y2 , \译码电路1_y3 , \译码电路1_y4 , \译码电路1_y5 , \译码电路1_y6 , \译码电路1_y7 ;
  wire [3:0] counter_1_q;

  Counter #(.width(4), .max('h9), .ongoal("wrap"), .trigger("rising"), .behavior("new")) counter_1 (
    .Q(counter_1_q), .clk(clock_1_out));  // open: load, D, count, carry, clr, preset, down
  Clock #(.highDuration(1), .lowDuration(1)) clock_1 (.out(clock_1_out));
  _7_segment \u_译码电路1  (
    .a(counter_1_q[3]), .b(counter_1_q[2]), .c(counter_1_q[1]), .d(counter_1_q[0]), .y1(\译码电路1_y1 ),
    .y2(\译码电路1_y2 ), .y3(\译码电路1_y3 ), .y4(\译码电路1_y4 ), .y5(\译码电路1_y5 ), .y6(\译码电路1_y6 ), .y7(\译码电路1_y7 ));
  _7_Segment_Display #(.active("true")) u_7_segment_display_1 (
    .g(\译码电路1_y7 ), .f(\译码电路1_y6 ), .a(\译码电路1_y1 ), .b(\译码电路1_y2 ), .e(\译码电路1_y5 ), .d(\译码电路1_y4 ),
    .c(\译码电路1_y3 ));  // open: dp
endmodule

module \实验2_红绿灯  (
);

  wire clock_1_out, dipswitch_1_p1, dipswitch_1_p2, dipswitch_2_p2, dipswitch_2_p4, G1, G2, R1, R2, T1, T2,
       Y1, Y2, \状态控制电路_s0 , \状态控制电路_s1 , \译码电路1_y1 , \译码电路1_y2 , \译码电路1_y3 , \译码电路1_y4 , \译码电路1_y5 ,
       \译码电路1_y6 , \译码电路1_y7 ;
  wire [3:0] counter_1_q;

  Counter #(.width(4), .max('h9), .ongoal("wrap"), .trigger("rising"), .behavior("new")) counter_1 (
    .Q(counter_1_q), .clk(clock_1_out));  // open: load, D, count, carry, clr, preset, down
  Clock #(.highDuration(1), .lowDuration(1)) clock_1 (.out(clock_1_out));
  // DipSwitch #(.NSwitches(1)) dipswitch_1: pin names not known; wires that end beside it: dipswitch_1_p1, dipswitch_1_p2, T1, dipswitch_1_p1
  _7_segment \u_译码电路1  (
    .a(counter_1_q[3]), .b(counter_1_q[2]), .c(counter_1_q[1]), .d(counter_1_q[0]), .y1(\译码电路1_y1 ),
    .y2(\译码电路1_y2 ), .y3(\译码电路1_y3 ), .y4(\译码电路1_y4 ), .y5(\译码电路1_y5 ), .y6(\译码电路1_y6 ), .y7(\译码电路1_y7 ));
  LED #(.active("true")) led_1 (.in(R1));
  LED #(.active("true")) led_2 (.in(Y1));
  LED #(.active("true")) led_3 (.in(G1));
  // DipSwitch #(.NSwitches(1)) dipswitch_2: pin names not known; wires that end beside it: dipswitch_1_p2, dipswitch_2_p2, T2, dipswitch_2_p4, dipswitch_2_p4, G2, dipswitch_2_p2, dipswitch_2_p4, dipswitch_2_p4
  FSM_new \u_状态控制电路  (.Ta(T1), .Tb(T2), .S1(\状态控制电路_s1 ), .S0(\状态控制电路_s0 ));
  LED #(.active("true")) led_4 (.in(R2));
  LED #(.active("true")) led_5 (.in(G2));
  LED #(.active("true")) led_6 (.in(Y2));
  _7_Segment_Display #(.active("true")) u_7_segment_display_1 (
    .g(\译码电路1_y7 ), .f(\译码电路1_y6 ), .a(\译码电路1_y1 ), .b(\译码电路1_y2 ), .e(\译码电路1_y5 ), .d(\译码电路1_y4 ),
    .c(\译码电路1_y3 ));  // open: dp
  \红绿灯控制电路  \u_红绿灯控制电路  (.S1(\状态控制电路_s1 ), .S0(\状态控制电路_s0 ), .R1(R1), .G1(G1), .Y1(Y1), .R2(R2), .G2(G2), .Y2(Y2));

  // Notes on the sheet:
  //   Ta
  //   Tb
  //   Ta
  //   Tb
endmodule

module \实验3_单周期CPU  (
  input  in_1,
  input  in_2,
  input  in_3
);

  wire ALUSrc, and_1_out, bitselector_1_out, Branch, CLK, halt, Jump, MemtoReg, MemWrite, not_1_out,
       not_2_out, RegDst, RegWrite, RESET_out, xor_1_out, \算术逻辑运算单元alu_1_结果是否为0 ;
  wire [2:0] ALUControl;
  wire [4:0] multiplexer_3_out;
  wire [27:2] \n32位地址总线32位数据总线rom存储器_1_data_bus_out ;
  wire [31:0] adder_1_out, adder_2_out, bit_extender_1_out, \mips寄存器文件_1_r_data1 , \mips寄存器文件_1_r_data2 ,
       multiplexer_1_out, multiplexer_2_out, multiplexer_4_out, multiplexer_5_out,
       \n32位地址总线32位数据总线ram存储器_1_data_bus_out , register_1_q, shifter_1_out, \算术逻辑运算单元alu_1_result ;
  wire [31:26] \n32位地址总线32位数据总线rom存储器_1_data_bus_out_2 ;

  Clock #(.highDuration(1), .lowDuration(1)) clock_1 (.out(CLK));
  Multiplexer #(.select(1), .width(32), .disabled("Z"), .enable("false")) multiplexer_1 (
    .in0(adder_1_out), .in1(adder_2_out), .out(multiplexer_1_out), .sel(and_1_out));
  not not_1 (not_1_out, halt);
  Register #(.width(32), .trigger("rising"), .Select("low")) register_1 (
    .D(multiplexer_2_out), .en(not_1_out), .Q(register_1_q), .clk(CLK), .clr(RESET_out));
  Multiplexer #(.select(1), .width(32), .disabled("Z"), .enable("false")) multiplexer_2 (
    .in0(multiplexer_1_out), .in1({adder_1_out[31:28], \n32位地址总线32位数据总线rom存储器_1_data_bus_out , 2'b00}),
    .out(multiplexer_2_out), .sel(Jump));
  Button RESET (.out(RESET_out));
  Adder #(.width(32)) adder_1 (.a(register_1_q), .b(32'h4), .out(adder_1_out));  // open: cin, cout
  \_32位地址总线32位数据总线ROM存储器  \u_32位地址总线32位数据总线rom存储器_1  (
    .CS(in_1), .Address_Bus(register_1_q),
    .Data_Bus_Out({\n32位地址总线32位数据总线rom存储器_1_data_bus_out_2 , \n32位地址总线32位数据总线rom存储器_1_data_bus_out }));
  ControlUnit controlunit_1 (
    .Op(\n32位地址总线32位数据总线rom存储器_1_data_bus_out_2 ), .Funct(\n32位地址总线32位数据总线rom存储器_1_data_bus_out [7:2]),
    .MemtoReg(MemtoReg), .MemWrite(MemWrite), .Branch(Branch), .ALUControl(ALUControl), .ALUSrc(ALUSrc),
    .RegDst(RegDst), .RegWrite(RegWrite), .Jump(Jump), .syscall(halt));
  \MIPS寄存器文件  \mips寄存器文件_1  (
    .A1_address(\n32位地址总线32位数据总线rom存储器_1_data_bus_out [27:23]), .W_data(multiplexer_5_out),
    .R_data1(\mips寄存器文件_1_r_data1 ), .R_data2(\mips寄存器文件_1_r_data2 ),
    .A2_address(\n32位地址总线32位数据总线rom存储器_1_data_bus_out [22:18]), .W_address(multiplexer_3_out),
    .W_Enable(RegWrite), .CLK(CLK));
  assign bit_extender_1_out = {{16{\n32位地址总线32位数据总线rom存储器_1_data_bus_out [17]}}, \n32位地址总线32位数据总线rom存储器_1_data_bus_out [17:2]};  // Bit_Extender bit_extender_1
  Multiplexer #(.select(1), .width(5), .disabled("Z"), .enable("false")) multiplexer_3 (
    .in0(\n32位地址总线32位数据总线rom存储器_1_data_bus_out [22:18]), .in1(\n32位地址总线32位数据总线rom存储器_1_data_bus_out [17:13]),
    .out(multiplexer_3_out), .sel(RegDst));
  Shifter #(.width(32), .shift("ll")) shifter_1 (.in(bit_extender_1_out), .\dist (5'b00010), .out(shifter_1_out));
  Adder #(.width(32)) adder_2 (.a(shifter_1_out), .b(adder_1_out), .out(adder_2_out));  // open: cin, cout
  Multiplexer #(.select(1), .width(32), .disabled("Z"), .enable("false")) multiplexer_4 (
    .in0(\mips寄存器文件_1_r_data2 ), .in1(bit_extender_1_out), .out(multiplexer_4_out), .sel(ALUSrc));
  BitSelector #(.width(6), .group(1)) bitselector_1 (
    .in(\n32位地址总线32位数据总线rom存储器_1_data_bus_out_2 ), .out(bitselector_1_out), .sel(3'b000));
  \算术逻辑运算单元ALU  \u_算术逻辑运算单元alu_1  (
    .AluOP(ALUControl), .X(\mips寄存器文件_1_r_data1 ), .Result(\算术逻辑运算单元alu_1_result ), .Y(multiplexer_4_out),
    .\结果是否为0 (\算术逻辑运算单元alu_1_结果是否为0 ));
  and and_1 (and_1_out, Branch, xor_1_out);
  xor xor_1 (xor_1_out, bitselector_1_out, \算术逻辑运算单元alu_1_结果是否为0 );
  not not_2 (not_2_out, MemWrite);
  \_32位地址总线32位数据总线RAM存储器  \u_32位地址总线32位数据总线ram存储器_1  (
    .CS(in_2), .Store(MemWrite), .CLK(CLK), .Address_Bus(\算术逻辑运算单元alu_1_result ),
    .Data_Bus_In(\mips寄存器文件_1_r_data2 ), .Load(not_2_out), .Clear(in_3),
    .Data_Bus_Out(\n32位地址总线32位数据总线ram存储器_1_data_bus_out ));
  Multiplexer #(.select(1), .width(32), .disabled("Z"), .enable("false")) multiplexer_5 (
    .in0(\算术逻辑运算单元alu_1_result ), .in1(\n32位地址总线32位数据总线ram存储器_1_data_bus_out ), .out(multiplexer_5_out),
    .sel(MemtoReg));
endmodule

module \MIPS寄存器文件  (
  input  [4:0] A1_address,
  input  [31:0] W_data,
  input  [4:0] A2_address,
  input  [4:0] W_address,
  input  W_Enable,
  input  CLK,
  output [31:0] R_data1,
  output [31:0] R_data2
);

  // RegisterFile registerfile_1: pin names not known; wires that end beside it: W_data, CLK, W_Enable, W_address, A1_address, A2_address, R_data1, R_data2

  // Other names for the same wires on the sheet: A1[4:0] = A1_address; A2[4:0] = A2_address; A3[4:0] = W_address;
  //   RD1[31:0] = R_data1; RD2[31:0] = R_data2; WD3[31:0] = W_data; WE3 = W_Enable
endmodule

module \_32位地址总线32位数据总线ROM存储器  (
  input  CS,
  input  [31:0] Address_Bus,
  output [31:0] Data_Bus_Out
);

  wire decoder_1_out0, decoder_1_out1, decoder_1_out2, decoder_1_out3, decoder_1_out4, decoder_1_out5,
       decoder_1_out6, decoder_1_out7, decoder_2_out0, decoder_2_out1, decoder_2_out2, decoder_2_out3,
       decoder_2_out4, decoder_2_out5, decoder_2_out6, decoder_2_out7, nand_1_out, nand_2_out, nand_3_out,
       nand_4_out, nand_5_out, nand_6_out, nand_7_out, nand_8_out, nand_9_out, nand_10_out, nand_11_out,
       nand_12_out, nand_13_out, nand_14_out, nand_15_out, nand_16_out, nand_17_out, nand_18_out,
       nand_19_out, nand_20_out, nand_21_out, nand_22_out, nand_23_out, nand_24_out, nand_25_out,
       nand_26_out, nand_27_out, nand_28_out, nand_29_out, nand_30_out, nand_31_out, nand_32_out,
       nand_33_out, nand_34_out, nand_35_out, nand_36_out, nand_37_out, nand_38_out, nand_39_out,
       nand_40_out, nand_41_out, nand_42_out, nand_43_out, nand_44_out, nand_45_out, nand_46_out,
       nand_47_out, nand_48_out, nand_49_out, nand_50_out, nand_51_out, nand_52_out, nand_53_out,
       nand_54_out, nand_55_out, nand_56_out, nand_57_out, nand_58_out, nand_59_out, nand_60_out,
       nand_61_out, nand_62_out, nand_63_out, nand_64_out, not_1_out;

  not not_1 (not_1_out, CS);
  Decoder #(.select(3), .tristate("false"), .disabled(0), .enable("true")) decoder_1 (
    .out0(decoder_1_out0), .out1(decoder_1_out1), .out2(decoder_1_out2), .out3(decoder_1_out3),
    .out4(decoder_1_out4), .out5(decoder_1_out5), .out6(decoder_1_out6), .out7(decoder_1_out7),
    .sel(Address_Bus[31:29]), .en(not_1_out));
  Decoder #(.select(3), .tristate("false"), .disabled(0), .enable("true")) decoder_2 (
    .out0(decoder_2_out0), .out1(decoder_2_out1), .out2(decoder_2_out2), .out3(decoder_2_out3),
    .out4(decoder_2_out4), .out5(decoder_2_out5), .out6(decoder_2_out6), .out7(decoder_2_out7),
    .sel(Address_Bus[28:26]), .en(not_1_out));
  nand nand_1 (nand_1_out, decoder_2_out0, decoder_1_out0);
  nand nand_2 (nand_2_out, decoder_2_out0, decoder_1_out1);
  nand nand_3 (nand_3_out, decoder_2_out0, decoder_1_out2);
  nand nand_4 (nand_4_out, decoder_2_out0, decoder_1_out3);
  nand nand_5 (nand_5_out, decoder_2_out0, decoder_1_out4);
  nand nand_6 (nand_6_out, decoder_2_out0, decoder_1_out5);
  nand nand_7 (nand_7_out, decoder_2_out0, decoder_1_out6);
  nand nand_8 (nand_8_out, decoder_2_out0, decoder_1_out7);
  ROM #(.addrWidth(24), .dataWidth(32), .Select("low")) rom_1 (
    .addr(Address_Bus[25:2]), .data(Data_Bus_Out), .sel(nand_1_out));
  ROM #(.addrWidth(24), .dataWidth(32), .Select("low")) rom_2 (
    .addr(Address_Bus[25:2]), .data(Data_Bus_Out), .sel(nand_2_out));
  ROM #(.addrWidth(24), .dataWidth(32), .Select("low")) rom_3 (
    .addr(Address_Bus[25:2]), .data(Data_Bus_Out), .sel(nand_3_out));
  ROM #(.addrWidth(24), .dataWidth(32), .Select("low")) rom_4 (
    .addr(Address_Bus[25:2]), .data(Data_Bus_Out), .sel(nand_4_out));
  ROM #(.addrWidth(24), .dataWidth(32), .Select("low")) rom_5 (
    .addr(Address_Bus[25:2]), .data(Data_Bus_Out), .sel(nand_5_out));
  ROM #(.addrWidth(24), .dataWidth(32), .Select("low")) rom_6 (
    .addr(Address_Bus[25:2]), .data(Data_Bus_Out), .sel(nand_6_out));
  ROM #(.addrWidth(24), .dataWidth(32), .Select("low")) rom_7 (
    .addr(Address_Bus[25:2]), .data(Data_Bus_Out), .sel(nand_7_out));
  ROM #(.addrWidth(24), .dataWidth(32), .Select("low")) rom_8 (
    .addr(Address_Bus[25:2]), .data(Data_Bus_Out), .sel(nand_8_out));
  nand nand_9 (nand_9_out, decoder_2_out1, decoder_1_out0);
  nand nand_10 (nand_10_out, decoder_2_out1, decoder_1_out1);
  nand nand_11 (nand_11_out, decoder_2_out1, decoder_1_out2);
  nand nand_12 (nand_12_out, decoder_2_out1, decoder_1_out3);
  nand nand_13 (nand_13_out, decoder_2_out1, decoder_1_out4);
  nand nand_14 (nand_14_out, decoder_2_out1, decoder_1_out5);
  nand nand_15 (nand_15_out, decoder_2_out1, decoder_1_out6);
  nand nand_16 (nand_16_out, decoder_2_out1, decoder_1_out7);
  ROM #(.addrWidth(24), .dataWidth(32), .Select("low")) rom_9 (
    .addr(Address_Bus[25:2]), .data(Data_Bus_Out), .sel(nand_9_out));
  ROM #(.addrWidth(24), .dataWidth(32), .Select("low")) rom_10 (
    .addr(Address_Bus[25:2]), .data(Data_Bus_Out), .sel(nand_10_out));
  ROM #(.addrWidth(24), .dataWidth(32), .Select("low")) rom_11 (
    .addr(Address_Bus[25:2]), .data(Data_Bus_Out), .sel(nand_11_out));
  ROM #(.addrWidth(24), .dataWidth(32), .Select("low")) rom_12 (
    .addr(Address_Bus[25:2]), .data(Data_Bus_Out), .sel(nand_12_out));
  ROM #(.addrWidth(24), .dataWidth(32), .Select("low")) rom_13 (
    .addr(Address_Bus[25:2]), .data(Data_Bus_Out), .sel(nand_13_out));
  ROM #(.addrWidth(24), .dataWidth(32), .Select("low")) rom_14 (
    .addr(Address_Bus[25:2]), .data(Data_Bus_Out), .sel(nand_14_out));
  ROM #(.addrWidth(24), .dataWidth(32), .Select("low")) rom_15 (
    .addr(Address_Bus[25:2]), .data(Data_Bus_Out), .sel(nand_15_out));
  ROM #(.addrWidth(24), .dataWidth(32), .Select("low")) rom_16 (
    .addr(Address_Bus[25:2]), .data(Data_Bus_Out), .sel(nand_16_out));
  nand nand_17 (nand_17_out, decoder_2_out2, decoder_1_out0);
  nand nand_18 (nand_18_out, decoder_2_out2, decoder_1_out1);
  nand nand_19 (nand_19_out, decoder_2_out2, decoder_1_out2);
  nand nand_20 (nand_20_out, decoder_2_out2, decoder_1_out3);
  nand nand_21 (nand_21_out, decoder_2_out2, decoder_1_out4);
  nand nand_22 (nand_22_out, decoder_2_out2, decoder_1_out5);
  nand nand_23 (nand_23_out, decoder_2_out2, decoder_1_out6);
  nand nand_24 (nand_24_out, decoder_2_out2, decoder_1_out7);
  ROM #(.addrWidth(24), .dataWidth(32), .Select("low")) rom_17 (
    .addr(Address_Bus[25:2]), .data(Data_Bus_Out), .sel(nand_17_out));
  ROM #(.addrWidth(24), .dataWidth(32), .Select("low")) rom_18 (
    .addr(Address_Bus[25:2]), .data(Data_Bus_Out), .sel(nand_18_out));
  ROM #(.addrWidth(24), .dataWidth(32), .Select("low")) rom_19 (
    .addr(Address_Bus[25:2]), .data(Data_Bus_Out), .sel(nand_19_out));
  ROM #(.addrWidth(24), .dataWidth(32), .Select("low")) rom_20 (
    .addr(Address_Bus[25:2]), .data(Data_Bus_Out), .sel(nand_20_out));
  ROM #(.addrWidth(24), .dataWidth(32), .Select("low")) rom_21 (
    .addr(Address_Bus[25:2]), .data(Data_Bus_Out), .sel(nand_21_out));
  ROM #(.addrWidth(24), .dataWidth(32), .Select("low")) rom_22 (
    .addr(Address_Bus[25:2]), .data(Data_Bus_Out), .sel(nand_22_out));
  ROM #(.addrWidth(24), .dataWidth(32), .Select("low")) rom_23 (
    .addr(Address_Bus[25:2]), .data(Data_Bus_Out), .sel(nand_23_out));
  ROM #(.addrWidth(24), .dataWidth(32), .Select("low")) rom_24 (
    .addr(Address_Bus[25:2]), .data(Data_Bus_Out), .sel(nand_24_out));
  nand nand_25 (nand_25_out, decoder_2_out3, decoder_1_out0);
  nand nand_26 (nand_26_out, decoder_2_out3, decoder_1_out1);
  nand nand_27 (nand_27_out, decoder_2_out3, decoder_1_out2);
  nand nand_28 (nand_28_out, decoder_2_out3, decoder_1_out3);
  nand nand_29 (nand_29_out, decoder_2_out3, decoder_1_out4);
  nand nand_30 (nand_30_out, decoder_2_out3, decoder_1_out5);
  nand nand_31 (nand_31_out, decoder_2_out3, decoder_1_out6);
  nand nand_32 (nand_32_out, decoder_2_out3, decoder_1_out7);
  ROM #(.addrWidth(24), .dataWidth(32), .Select("low")) rom_25 (
    .addr(Address_Bus[25:2]), .data(Data_Bus_Out), .sel(nand_25_out));
  ROM #(.addrWidth(24), .dataWidth(32), .Select("low")) rom_26 (
    .addr(Address_Bus[25:2]), .data(Data_Bus_Out), .sel(nand_26_out));
  ROM #(.addrWidth(24), .dataWidth(32), .Select("low")) rom_27 (
    .addr(Address_Bus[25:2]), .data(Data_Bus_Out), .sel(nand_27_out));
  ROM #(.addrWidth(24), .dataWidth(32), .Select("low")) rom_28 (
    .addr(Address_Bus[25:2]), .data(Data_Bus_Out), .sel(nand_28_out));
  ROM #(.addrWidth(24), .dataWidth(32), .Select("low")) rom_29 (
    .addr(Address_Bus[25:2]), .data(Data_Bus_Out), .sel(nand_29_out));
  ROM #(.addrWidth(24), .dataWidth(32), .Select("low")) rom_30 (
    .addr(Address_Bus[25:2]), .data(Data_Bus_Out), .sel(nand_30_out));
  ROM #(.addrWidth(24), .dataWidth(32), .Select("low")) rom_31 (
    .addr(Address_Bus[25:2]), .data(Data_Bus_Out), .sel(nand_31_out));
  ROM #(.addrWidth(24), .dataWidth(32), .Select("low")) rom_32 (
    .addr(Address_Bus[25:2]), .data(Data_Bus_Out), .sel(nand_32_out));
  nand nand_33 (nand_33_out, decoder_2_out4, decoder_1_out0);
  nand nand_34 (nand_34_out, decoder_2_out4, decoder_1_out1);
  nand nand_35 (nand_35_out, decoder_2_out4, decoder_1_out2);
  nand nand_36 (nand_36_out, decoder_2_out4, decoder_1_out3);
  nand nand_37 (nand_37_out, decoder_2_out4, decoder_1_out4);
  nand nand_38 (nand_38_out, decoder_2_out4, decoder_1_out5);
  nand nand_39 (nand_39_out, decoder_2_out4, decoder_1_out6);
  nand nand_40 (nand_40_out, decoder_2_out4, decoder_1_out7);
  ROM #(.addrWidth(24), .dataWidth(32), .Select("low")) rom_33 (
    .addr(Address_Bus[25:2]), .data(Data_Bus_Out), .sel(nand_33_out));
  ROM #(.addrWidth(24), .dataWidth(32), .Select("low")) rom_34 (
    .addr(Address_Bus[25:2]), .data(Data_Bus_Out), .sel(nand_34_out));
  ROM #(.addrWidth(24), .dataWidth(32), .Select("low")) rom_35 (
    .addr(Address_Bus[25:2]), .data(Data_Bus_Out), .sel(nand_35_out));
  ROM #(.addrWidth(24), .dataWidth(32), .Select("low")) rom_36 (
    .addr(Address_Bus[25:2]), .data(Data_Bus_Out), .sel(nand_36_out));
  ROM #(.addrWidth(24), .dataWidth(32), .Select("low")) rom_37 (
    .addr(Address_Bus[25:2]), .data(Data_Bus_Out), .sel(nand_37_out));
  ROM #(.addrWidth(24), .dataWidth(32), .Select("low")) rom_38 (
    .addr(Address_Bus[25:2]), .data(Data_Bus_Out), .sel(nand_38_out));
  ROM #(.addrWidth(24), .dataWidth(32), .Select("low")) rom_39 (
    .addr(Address_Bus[25:2]), .data(Data_Bus_Out), .sel(nand_39_out));
  ROM #(.addrWidth(24), .dataWidth(32), .Select("low")) rom_40 (
    .addr(Address_Bus[25:2]), .data(Data_Bus_Out), .sel(nand_40_out));
  nand nand_41 (nand_41_out, decoder_2_out5, decoder_1_out0);
  nand nand_42 (nand_42_out, decoder_2_out5, decoder_1_out1);
  nand nand_43 (nand_43_out, decoder_2_out5, decoder_1_out2);
  nand nand_44 (nand_44_out, decoder_2_out5, decoder_1_out3);
  nand nand_45 (nand_45_out, decoder_2_out5, decoder_1_out4);
  nand nand_46 (nand_46_out, decoder_2_out5, decoder_1_out5);
  nand nand_47 (nand_47_out, decoder_2_out5, decoder_1_out6);
  nand nand_48 (nand_48_out, decoder_2_out5, decoder_1_out7);
  ROM #(.addrWidth(24), .dataWidth(32), .Select("low")) rom_41 (
    .addr(Address_Bus[25:2]), .data(Data_Bus_Out), .sel(nand_41_out));
  ROM #(.addrWidth(24), .dataWidth(32), .Select("low")) rom_42 (
    .addr(Address_Bus[25:2]), .data(Data_Bus_Out), .sel(nand_42_out));
  ROM #(.addrWidth(24), .dataWidth(32), .Select("low")) rom_43 (
    .addr(Address_Bus[25:2]), .data(Data_Bus_Out), .sel(nand_43_out));
  ROM #(.addrWidth(24), .dataWidth(32), .Select("low")) rom_44 (
    .addr(Address_Bus[25:2]), .data(Data_Bus_Out), .sel(nand_44_out));
  ROM #(.addrWidth(24), .dataWidth(32), .Select("low")) rom_45 (
    .addr(Address_Bus[25:2]), .data(Data_Bus_Out), .sel(nand_45_out));
  ROM #(.addrWidth(24), .dataWidth(32), .Select("low")) rom_46 (
    .addr(Address_Bus[25:2]), .data(Data_Bus_Out), .sel(nand_46_out));
  ROM #(.addrWidth(24), .dataWidth(32), .Select("low")) rom_47 (
    .addr(Address_Bus[25:2]), .data(Data_Bus_Out), .sel(nand_47_out));
  ROM #(.addrWidth(24), .dataWidth(32), .Select("low")) rom_48 (
    .addr(Address_Bus[25:2]), .data(Data_Bus_Out), .sel(nand_48_out));
  nand nand_49 (nand_49_out, decoder_2_out6, decoder_1_out0);
  nand nand_50 (nand_50_out, decoder_2_out6, decoder_1_out1);
  nand nand_51 (nand_51_out, decoder_2_out6, decoder_1_out2);
  nand nand_52 (nand_52_out, decoder_2_out6, decoder_1_out3);
  nand nand_53 (nand_53_out, decoder_2_out6, decoder_1_out4);
  nand nand_54 (nand_54_out, decoder_2_out6, decoder_1_out5);
  nand nand_55 (nand_55_out, decoder_2_out6, decoder_1_out6);
  nand nand_56 (nand_56_out, decoder_2_out6, decoder_1_out7);
  ROM #(.addrWidth(24), .dataWidth(32), .Select("low")) rom_49 (
    .addr(Address_Bus[25:2]), .data(Data_Bus_Out), .sel(nand_49_out));
  ROM #(.addrWidth(24), .dataWidth(32), .Select("low")) rom_50 (
    .addr(Address_Bus[25:2]), .data(Data_Bus_Out), .sel(nand_50_out));
  ROM #(.addrWidth(24), .dataWidth(32), .Select("low")) rom_51 (
    .addr(Address_Bus[25:2]), .data(Data_Bus_Out), .sel(nand_51_out));
  ROM #(.addrWidth(24), .dataWidth(32), .Select("low")) rom_52 (
    .addr(Address_Bus[25:2]), .data(Data_Bus_Out), .sel(nand_52_out));
  ROM #(.addrWidth(24), .dataWidth(32), .Select("low")) rom_53 (
    .addr(Address_Bus[25:2]), .data(Data_Bus_Out), .sel(nand_53_out));
  ROM #(.addrWidth(24), .dataWidth(32), .Select("low")) rom_54 (
    .addr(Address_Bus[25:2]), .data(Data_Bus_Out), .sel(nand_54_out));
  ROM #(.addrWidth(24), .dataWidth(32), .Select("low")) rom_55 (
    .addr(Address_Bus[25:2]), .data(Data_Bus_Out), .sel(nand_55_out));
  ROM #(.addrWidth(24), .dataWidth(32), .Select("low")) rom_56 (
    .addr(Address_Bus[25:2]), .data(Data_Bus_Out), .sel(nand_56_out));
  nand nand_57 (nand_57_out, decoder_2_out7, decoder_1_out0);
  nand nand_58 (nand_58_out, decoder_2_out7, decoder_1_out1);
  nand nand_59 (nand_59_out, decoder_2_out7, decoder_1_out2);
  nand nand_60 (nand_60_out, decoder_2_out7, decoder_1_out3);
  nand nand_61 (nand_61_out, decoder_2_out7, decoder_1_out4);
  nand nand_62 (nand_62_out, decoder_2_out7, decoder_1_out5);
  nand nand_63 (nand_63_out, decoder_2_out7, decoder_1_out6);
  nand nand_64 (nand_64_out, decoder_2_out7, decoder_1_out7);
  ROM #(.addrWidth(24), .dataWidth(32), .Select("low")) rom_57 (
    .addr(Address_Bus[25:2]), .data(Data_Bus_Out), .sel(nand_57_out));
  ROM #(.addrWidth(24), .dataWidth(32), .Select("low")) rom_58 (
    .addr(Address_Bus[25:2]), .data(Data_Bus_Out), .sel(nand_58_out));
  ROM #(.addrWidth(24), .dataWidth(32), .Select("low")) rom_59 (
    .addr(Address_Bus[25:2]), .data(Data_Bus_Out), .sel(nand_59_out));
  ROM #(.addrWidth(24), .dataWidth(32), .Select("low")) rom_60 (
    .addr(Address_Bus[25:2]), .data(Data_Bus_Out), .sel(nand_60_out));
  ROM #(.addrWidth(24), .dataWidth(32), .Select("low")) rom_61 (
    .addr(Address_Bus[25:2]), .data(Data_Bus_Out), .sel(nand_61_out));
  ROM #(.addrWidth(24), .dataWidth(32), .Select("low")) rom_62 (
    .addr(Address_Bus[25:2]), .data(Data_Bus_Out), .sel(nand_62_out));
  ROM #(.addrWidth(24), .dataWidth(32), .Select("low")) rom_63 (
    .addr(Address_Bus[25:2]), .data(Data_Bus_Out), .sel(nand_63_out));
  ROM #(.addrWidth(24), .dataWidth(32), .Select("low")) rom_64 (
    .addr(Address_Bus[25:2]), .data(Data_Bus_Out), .sel(nand_64_out));

  // Other names for the same wires on the sheet: Ad_TP[31:0] = Address_Bus; tunnel[23:0] = Address_Bus[25:2];
  //   DataOut[31:0] = Data_Bus_Out

  // Notes on the sheet:
  //   contents of rom_1 (hex, n*v repeats v):
  //   20100001 20110000 ae300000 22100001 22310004 ae300000 22100001 22310004 ae300000 22100001 22310004
  //   ae300000 22100001 22310004 ae300000 22100001 22310004 ae300000 22100001 22310004 ae300000 22100001
  //   22310004 ae300000 8020 2011001c 8e130000 8e340000 274402a 11000002 ae330000 ae140000 2231fffc
  //   1611fff8 22100004 2011001c 1611fff5 c
  //   外部各接口定义与原ROM相同
  //   按照字节编址，但按照字对齐访问
  //   contents of rom_9 (hex, n*v repeats v):
  //   7*0 ae300001 12150004 5*0 230b02a 8e320001
endmodule

module \_32位地址总线32位数据总线RAM存储器  (
  input  CS,
  input  Store,
  input  CLK,
  input  [31:0] Address_Bus,
  input  [31:0] Data_Bus_In,
  input  Load,
  input  Clear,
  output [31:0] Data_Bus_Out
);

  wire decoder_1_out0, decoder_1_out1, decoder_1_out2, decoder_1_out3, decoder_1_out4, decoder_1_out5,
       decoder_1_out6, decoder_1_out7, decoder_2_out0, decoder_2_out1, decoder_2_out2, decoder_2_out3,
       decoder_2_out4, decoder_2_out5, decoder_2_out6, decoder_2_out7, nand_1_out, nand_2_out, nand_3_out,
       nand_4_out, nand_5_out, nand_6_out, nand_7_out, nand_8_out, nand_9_out, nand_10_out, nand_11_out,
       nand_12_out, nand_13_out, nand_14_out, nand_15_out, nand_16_out, nand_17_out, nand_18_out,
       nand_19_out, nand_20_out, nand_21_out, nand_22_out, nand_23_out, nand_24_out, nand_25_out,
       nand_26_out, nand_27_out, nand_28_out, nand_29_out, nand_30_out, nand_31_out, nand_32_out,
       nand_33_out, nand_34_out, nand_35_out, nand_36_out, nand_37_out, nand_38_out, nand_39_out,
       nand_40_out, nand_41_out, nand_42_out, nand_43_out, nand_44_out, nand_45_out, nand_46_out,
       nand_47_out, nand_48_out, nand_49_out, nand_50_out, nand_51_out, nand_52_out, nand_53_out,
       nand_54_out, nand_55_out, nand_56_out, nand_57_out, nand_58_out, nand_59_out, nand_60_out,
       nand_61_out, nand_62_out, nand_63_out, nand_64_out, not_1_out;

  Decoder #(.select(3), .tristate("false"), .disabled(0), .enable("true")) decoder_1 (
    .out0(decoder_1_out0), .out1(decoder_1_out1), .out2(decoder_1_out2), .out3(decoder_1_out3),
    .out4(decoder_1_out4), .out5(decoder_1_out5), .out6(decoder_1_out6), .out7(decoder_1_out7),
    .sel(Address_Bus[31:29]), .en(not_1_out));
  not not_1 (not_1_out, CS);
  Decoder #(.select(3), .tristate("false"), .disabled(0), .enable("true")) decoder_2 (
    .out0(decoder_2_out0), .out1(decoder_2_out1), .out2(decoder_2_out2), .out3(decoder_2_out3),
    .out4(decoder_2_out4), .out5(decoder_2_out5), .out6(decoder_2_out6), .out7(decoder_2_out7),
    .sel(Address_Bus[28:26]), .en(not_1_out));
  nand nand_1 (nand_1_out, decoder_2_out0, decoder_1_out0);
  nand nand_2 (nand_2_out, decoder_2_out0, decoder_1_out1);
  nand nand_3 (nand_3_out, decoder_2_out0, decoder_1_out2);
  nand nand_4 (nand_4_out, decoder_2_out0, decoder_1_out3);
  nand nand_5 (nand_5_out, decoder_2_out0, decoder_1_out4);
  nand nand_6 (nand_6_out, decoder_2_out0, decoder_1_out5);
  nand nand_7 (nand_7_out, decoder_2_out0, decoder_1_out6);
  nand nand_8 (nand_8_out, decoder_2_out0, decoder_1_out7);
  RAM #(.addrWidth(24), .dataWidth(32), .bus("separate"), .Select("low")) ram_1 (
    .addr(Address_Bus[25:2]), .din(Data_Bus_In), .data(Data_Bus_Out), .str(Store), .sel(nand_1_out),
    .clk(CLK), .ld(Load), .clr(Clear));
  RAM #(.addrWidth(24), .dataWidth(32), .bus("separate"), .Select("low")) ram_2 (
    .addr(Address_Bus[25:2]), .din(Data_Bus_In), .data(Data_Bus_Out), .str(Store), .sel(nand_2_out),
    .clk(CLK), .ld(Load), .clr(Clear));
  RAM #(.addrWidth(24), .dataWidth(32), .bus("separate"), .Select("low")) ram_3 (
    .addr(Address_Bus[25:2]), .din(Data_Bus_In), .data(Data_Bus_Out), .str(Store), .sel(nand_3_out),
    .clk(CLK), .ld(Load), .clr(Clear));
  RAM #(.addrWidth(24), .dataWidth(32), .bus("separate"), .Select("low")) ram_4 (
    .addr(Address_Bus[25:2]), .din(Data_Bus_In), .data(Data_Bus_Out), .str(Store), .sel(nand_4_out),
    .clk(CLK), .ld(Load), .clr(Clear));
  RAM #(.addrWidth(24), .dataWidth(32), .bus("separate"), .Select("low")) ram_5 (
    .addr(Address_Bus[25:2]), .din(Data_Bus_In), .data(Data_Bus_Out), .str(Store), .sel(nand_5_out),
    .clk(CLK), .ld(Load), .clr(Clear));
  RAM #(.addrWidth(24), .dataWidth(32), .bus("separate"), .Select("low")) ram_6 (
    .addr(Address_Bus[25:2]), .din(Data_Bus_In), .data(Data_Bus_Out), .str(Store), .sel(nand_6_out),
    .clk(CLK), .ld(Load), .clr(Clear));
  RAM #(.addrWidth(24), .dataWidth(32), .bus("separate"), .Select("low")) ram_7 (
    .addr(Address_Bus[25:2]), .din(Data_Bus_In), .data(Data_Bus_Out), .str(Store), .sel(nand_7_out),
    .clk(CLK), .ld(Load), .clr(Clear));
  RAM #(.addrWidth(24), .dataWidth(32), .bus("separate"), .Select("low")) ram_8 (
    .addr(Address_Bus[25:2]), .din(Data_Bus_In), .data(Data_Bus_Out), .str(Store), .sel(nand_8_out),
    .clk(CLK), .ld(Load), .clr(Clear));
  nand nand_9 (nand_9_out, decoder_2_out1, decoder_1_out0);
  nand nand_10 (nand_10_out, decoder_2_out1, decoder_1_out1);
  nand nand_11 (nand_11_out, decoder_2_out1, decoder_1_out2);
  nand nand_12 (nand_12_out, decoder_2_out1, decoder_1_out3);
  nand nand_13 (nand_13_out, decoder_2_out1, decoder_1_out4);
  nand nand_14 (nand_14_out, decoder_2_out1, decoder_1_out5);
  nand nand_15 (nand_15_out, decoder_2_out1, decoder_1_out6);
  nand nand_16 (nand_16_out, decoder_2_out1, decoder_1_out7);
  RAM #(.addrWidth(24), .dataWidth(32), .bus("separate"), .Select("low")) ram_9 (
    .addr(Address_Bus[25:2]), .din(Data_Bus_In), .data(Data_Bus_Out), .str(Store), .sel(nand_9_out),
    .clk(CLK), .ld(Load), .clr(Clear));
  RAM #(.addrWidth(24), .dataWidth(32), .bus("separate"), .Select("low")) ram_10 (
    .addr(Address_Bus[25:2]), .din(Data_Bus_In), .data(Data_Bus_Out), .str(Store), .sel(nand_10_out),
    .clk(CLK), .ld(Load), .clr(Clear));
  RAM #(.addrWidth(24), .dataWidth(32), .bus("separate"), .Select("low")) ram_11 (
    .addr(Address_Bus[25:2]), .din(Data_Bus_In), .data(Data_Bus_Out), .str(Store), .sel(nand_11_out),
    .clk(CLK), .ld(Load), .clr(Clear));
  RAM #(.addrWidth(24), .dataWidth(32), .bus("separate"), .Select("low")) ram_12 (
    .addr(Address_Bus[25:2]), .din(Data_Bus_In), .data(Data_Bus_Out), .str(Store), .sel(nand_12_out),
    .clk(CLK), .ld(Load), .clr(Clear));
  RAM #(.addrWidth(24), .dataWidth(32), .bus("separate"), .Select("low")) ram_13 (
    .addr(Address_Bus[25:2]), .din(Data_Bus_In), .data(Data_Bus_Out), .str(Store), .sel(nand_13_out),
    .clk(CLK), .ld(Load), .clr(Clear));
  RAM #(.addrWidth(24), .dataWidth(32), .bus("separate"), .Select("low")) ram_14 (
    .addr(Address_Bus[25:2]), .din(Data_Bus_In), .data(Data_Bus_Out), .str(Store), .sel(nand_14_out),
    .clk(CLK), .ld(Load), .clr(Clear));
  RAM #(.addrWidth(24), .dataWidth(32), .bus("separate"), .Select("low")) ram_15 (
    .addr(Address_Bus[25:2]), .din(Data_Bus_In), .data(Data_Bus_Out), .str(Store), .sel(nand_15_out),
    .clk(CLK), .ld(Load), .clr(Clear));
  RAM #(.addrWidth(24), .dataWidth(32), .bus("separate"), .Select("low")) ram_16 (
    .addr(Address_Bus[25:2]), .din(Data_Bus_In), .data(Data_Bus_Out), .str(Store), .sel(nand_16_out),
    .clk(CLK), .ld(Load), .clr(Clear));
  nand nand_17 (nand_17_out, decoder_2_out2, decoder_1_out0);
  nand nand_18 (nand_18_out, decoder_2_out2, decoder_1_out1);
  nand nand_19 (nand_19_out, decoder_2_out2, decoder_1_out2);
  nand nand_20 (nand_20_out, decoder_2_out2, decoder_1_out3);
  nand nand_21 (nand_21_out, decoder_2_out2, decoder_1_out4);
  nand nand_22 (nand_22_out, decoder_2_out2, decoder_1_out5);
  nand nand_23 (nand_23_out, decoder_2_out2, decoder_1_out6);
  nand nand_24 (nand_24_out, decoder_2_out2, decoder_1_out7);
  RAM #(.addrWidth(24), .dataWidth(32), .bus("separate"), .Select("low")) ram_17 (
    .addr(Address_Bus[25:2]), .din(Data_Bus_In), .data(Data_Bus_Out), .str(Store), .sel(nand_17_out),
    .clk(CLK), .ld(Load), .clr(Clear));
  RAM #(.addrWidth(24), .dataWidth(32), .bus("separate"), .Select("low")) ram_18 (
    .addr(Address_Bus[25:2]), .din(Data_Bus_In), .data(Data_Bus_Out), .str(Store), .sel(nand_18_out),
    .clk(CLK), .ld(Load), .clr(Clear));
  RAM #(.addrWidth(24), .dataWidth(32), .bus("separate"), .Select("low")) ram_19 (
    .addr(Address_Bus[25:2]), .din(Data_Bus_In), .data(Data_Bus_Out), .str(Store), .sel(nand_19_out),
    .clk(CLK), .ld(Load), .clr(Clear));
  RAM #(.addrWidth(24), .dataWidth(32), .bus("separate"), .Select("low")) ram_20 (
    .addr(Address_Bus[25:2]), .din(Data_Bus_In), .data(Data_Bus_Out), .str(Store), .sel(nand_20_out),
    .clk(CLK), .ld(Load), .clr(Clear));
  RAM #(.addrWidth(24), .dataWidth(32), .bus("separate"), .Select("low")) ram_21 (
    .addr(Address_Bus[25:2]), .din(Data_Bus_In), .data(Data_Bus_Out), .str(Store), .sel(nand_21_out),
    .clk(CLK), .ld(Load), .clr(Clear));
  RAM #(.addrWidth(24), .dataWidth(32), .bus("separate"), .Select("low")) ram_22 (
    .addr(Address_Bus[25:2]), .din(Data_Bus_In), .data(Data_Bus_Out), .str(Store), .sel(nand_22_out),
    .clk(CLK), .ld(Load), .clr(Clear));
  RAM #(.addrWidth(24), .dataWidth(32), .bus("separate"), .Select("low")) ram_23 (
    .addr(Address_Bus[25:2]), .din(Data_Bus_In), .data(Data_Bus_Out), .str(Store), .sel(nand_23_out),
    .clk(CLK), .ld(Load), .clr(Clear));
  RAM #(.addrWidth(24), .dataWidth(32), .bus("separate"), .Select("low")) ram_24 (
    .addr(Address_Bus[25:2]), .din(Data_Bus_In), .data(Data_Bus_Out), .str(Store), .sel(nand_24_out),
    .clk(CLK), .ld(Load), .clr(Clear));
  nand nand_25 (nand_25_out, decoder_2_out3, decoder_1_out0);
  nand nand_26 (nand_26_out, decoder_2_out3, decoder_1_out1);
  nand nand_27 (nand_27_out, decoder_2_out3, decoder_1_out2);
  nand nand_28 (nand_28_out, decoder_2_out3, decoder_1_out3);
  nand nand_29 (nand_29_out, decoder_2_out3, decoder_1_out4);
  nand nand_30 (nand_30_out, decoder_2_out3, decoder_1_out5);
  nand nand_31 (nand_31_out, decoder_2_out3, decoder_1_out6);
  nand nand_32 (nand_32_out, decoder_2_out3, decoder_1_out7);
  RAM #(.addrWidth(24), .dataWidth(32), .bus("separate"), .Select("low")) ram_25 (
    .addr(Address_Bus[25:2]), .din(Data_Bus_In), .data(Data_Bus_Out), .str(Store), .sel(nand_25_out),
    .clk(CLK), .ld(Load), .clr(Clear));
  RAM #(.addrWidth(24), .dataWidth(32), .bus("separate"), .Select("low")) ram_26 (
    .addr(Address_Bus[25:2]), .din(Data_Bus_In), .data(Data_Bus_Out), .str(Store), .sel(nand_26_out),
    .clk(CLK), .ld(Load), .clr(Clear));
  RAM #(.addrWidth(24), .dataWidth(32), .bus("separate"), .Select("low")) ram_27 (
    .addr(Address_Bus[25:2]), .din(Data_Bus_In), .data(Data_Bus_Out), .str(Store), .sel(nand_27_out),
    .clk(CLK), .ld(Load), .clr(Clear));
  RAM #(.addrWidth(24), .dataWidth(32), .bus("separate"), .Select("low")) ram_28 (
    .addr(Address_Bus[25:2]), .din(Data_Bus_In), .data(Data_Bus_Out), .str(Store), .sel(nand_28_out),
    .clk(CLK), .ld(Load), .clr(Clear));
  RAM #(.addrWidth(24), .dataWidth(32), .bus("separate"), .Select("low")) ram_29 (
    .addr(Address_Bus[25:2]), .din(Data_Bus_In), .data(Data_Bus_Out), .str(Store), .sel(nand_29_out),
    .clk(CLK), .ld(Load), .clr(Clear));
  RAM #(.addrWidth(24), .dataWidth(32), .bus("separate"), .Select("low")) ram_30 (
    .addr(Address_Bus[25:2]), .din(Data_Bus_In), .data(Data_Bus_Out), .str(Store), .sel(nand_30_out),
    .clk(CLK), .ld(Load), .clr(Clear));
  RAM #(.addrWidth(24), .dataWidth(32), .bus("separate"), .Select("low")) ram_31 (
    .addr(Address_Bus[25:2]), .din(Data_Bus_In), .data(Data_Bus_Out), .str(Store), .sel(nand_31_out),
    .clk(CLK), .ld(Load), .clr(Clear));
  RAM #(.addrWidth(24), .dataWidth(32), .bus("separate"), .Select("low")) ram_32 (
    .addr(Address_Bus[25:2]), .din(Data_Bus_In), .data(Data_Bus_Out), .str(Store), .sel(nand_32_out),
    .clk(CLK), .ld(Load), .clr(Clear));
  nand nand_33 (nand_33_out, decoder_2_out4, decoder_1_out0);
  nand nand_34 (nand_34_out, decoder_2_out4, decoder_1_out1);
  nand nand_35 (nand_35_out, decoder_2_out4, decoder_1_out2);
  nand nand_36 (nand_36_out, decoder_2_out4, decoder_1_out3);
  nand nand_37 (nand_37_out, decoder_2_out4, decoder_1_out4);
  nand nand_38 (nand_38_out, decoder_2_out4, decoder_1_out5);
  nand nand_39 (nand_39_out, decoder_2_out4, decoder_1_out6);
  nand nand_40 (nand_40_out, decoder_2_out4, decoder_1_out7);
  RAM #(.addrWidth(24), .dataWidth(32), .bus("separate"), .Select("low")) ram_33 (
    .addr(Address_Bus[25:2]), .din(Data_Bus_In), .data(Data_Bus_Out), .str(Store), .sel(nand_33_out),
    .clk(CLK), .ld(Load), .clr(Clear));
  RAM #(.addrWidth(24), .dataWidth(32), .bus("separate"), .Select("low")) ram_34 (
    .addr(Address_Bus[25:2]), .din(Data_Bus_In), .data(Data_Bus_Out), .str(Store), .sel(nand_34_out),
    .clk(CLK), .ld(Load), .clr(Clear));
  RAM #(.addrWidth(24), .dataWidth(32), .bus("separate"), .Select("low")) ram_35 (
    .addr(Address_Bus[25:2]), .din(Data_Bus_In), .data(Data_Bus_Out), .str(Store), .sel(nand_35_out),
    .clk(CLK), .ld(Load), .clr(Clear));
  RAM #(.addrWidth(24), .dataWidth(32), .bus("separate"), .Select("low")) ram_36 (
    .addr(Address_Bus[25:2]), .din(Data_Bus_In), .data(Data_Bus_Out), .str(Store), .sel(nand_36_out),
    .clk(CLK), .ld(Load), .clr(Clear));
  RAM #(.addrWidth(24), .dataWidth(32), .bus("separate"), .Select("low")) ram_37 (
    .addr(Address_Bus[25:2]), .din(Data_Bus_In), .data(Data_Bus_Out), .str(Store), .sel(nand_37_out),
    .clk(CLK), .ld(Load), .clr(Clear));
  RAM #(.addrWidth(24), .dataWidth(32), .bus("separate"), .Select("low")) ram_38 (
    .addr(Address_Bus[25:2]), .din(Data_Bus_In), .data(Data_Bus_Out), .str(Store), .sel(nand_38_out),
    .clk(CLK), .ld(Load), .clr(Clear));
  RAM #(.addrWidth(24), .dataWidth(32), .bus("separate"), .Select("low")) ram_39 (
    .addr(Address_Bus[25:2]), .din(Data_Bus_In), .data(Data_Bus_Out), .str(Store), .sel(nand_39_out),
    .clk(CLK), .ld(Load), .clr(Clear));
  RAM #(.addrWidth(24), .dataWidth(32), .bus("separate"), .Select("low")) ram_40 (
    .addr(Address_Bus[25:2]), .din(Data_Bus_In), .data(Data_Bus_Out), .str(Store), .sel(nand_40_out),
    .clk(CLK), .ld(Load), .clr(Clear));
  nand nand_41 (nand_41_out, decoder_2_out5, decoder_1_out0);
  nand nand_42 (nand_42_out, decoder_2_out5, decoder_1_out1);
  nand nand_43 (nand_43_out, decoder_2_out5, decoder_1_out2);
  nand nand_44 (nand_44_out, decoder_2_out5, decoder_1_out3);
  nand nand_45 (nand_45_out, decoder_2_out5, decoder_1_out4);
  nand nand_46 (nand_46_out, decoder_2_out5, decoder_1_out5);
  nand nand_47 (nand_47_out, decoder_2_out5, decoder_1_out6);
  nand nand_48 (nand_48_out, decoder_2_out5, decoder_1_out7);
  RAM #(.addrWidth(24), .dataWidth(32), .bus("separate"), .Select("low")) ram_41 (
    .addr(Address_Bus[25:2]), .din(Data_Bus_In), .data(Data_Bus_Out), .str(Store), .sel(nand_41_out),
    .clk(CLK), .ld(Load), .clr(Clear));
  RAM #(.addrWidth(24), .dataWidth(32), .bus("separate"), .Select("low")) ram_42 (
    .addr(Address_Bus[25:2]), .din(Data_Bus_In), .data(Data_Bus_Out), .str(Store), .sel(nand_42_out),
    .clk(CLK), .ld(Load), .clr(Clear));
  RAM #(.addrWidth(24), .dataWidth(32), .bus("separate"), .Select("low")) ram_43 (
    .addr(Address_Bus[25:2]), .din(Data_Bus_In), .data(Data_Bus_Out), .str(Store), .sel(nand_43_out),
    .clk(CLK), .ld(Load), .clr(Clear));
  RAM #(.addrWidth(24), .dataWidth(32), .bus("separate"), .Select("low")) ram_44 (
    .addr(Address_Bus[25:2]), .din(Data_Bus_In), .data(Data_Bus_Out), .str(Store), .sel(nand_44_out),
    .clk(CLK), .ld(Load), .clr(Clear));
  RAM #(.addrWidth(24), .dataWidth(32), .bus("separate"), .Select("low")) ram_45 (
    .addr(Address_Bus[25:2]), .din(Data_Bus_In), .data(Data_Bus_Out), .str(Store), .sel(nand_45_out),
    .clk(CLK), .ld(Load), .clr(Clear));
  RAM #(.addrWidth(24), .dataWidth(32), .bus("separate"), .Select("low")) ram_46 (
    .addr(Address_Bus[25:2]), .din(Data_Bus_In), .data(Data_Bus_Out), .str(Store), .sel(nand_46_out),
    .clk(CLK), .ld(Load), .clr(Clear));
  RAM #(.addrWidth(24), .dataWidth(32), .bus("separate"), .Select("low")) ram_47 (
    .addr(Address_Bus[25:2]), .din(Data_Bus_In), .data(Data_Bus_Out), .str(Store), .sel(nand_47_out),
    .clk(CLK), .ld(Load), .clr(Clear));
  RAM #(.addrWidth(24), .dataWidth(32), .bus("separate"), .Select("low")) ram_48 (
    .addr(Address_Bus[25:2]), .din(Data_Bus_In), .data(Data_Bus_Out), .str(Store), .sel(nand_48_out),
    .clk(CLK), .ld(Load), .clr(Clear));
  nand nand_49 (nand_49_out, decoder_2_out6, decoder_1_out0);
  nand nand_50 (nand_50_out, decoder_2_out6, decoder_1_out1);
  nand nand_51 (nand_51_out, decoder_2_out6, decoder_1_out2);
  nand nand_52 (nand_52_out, decoder_2_out6, decoder_1_out3);
  nand nand_53 (nand_53_out, decoder_2_out6, decoder_1_out4);
  nand nand_54 (nand_54_out, decoder_2_out6, decoder_1_out5);
  nand nand_55 (nand_55_out, decoder_2_out6, decoder_1_out6);
  nand nand_56 (nand_56_out, decoder_2_out6, decoder_1_out7);
  RAM #(.addrWidth(24), .dataWidth(32), .bus("separate"), .Select("low")) ram_49 (
    .addr(Address_Bus[25:2]), .din(Data_Bus_In), .data(Data_Bus_Out), .str(Store), .sel(nand_49_out),
    .clk(CLK), .ld(Load), .clr(Clear));
  RAM #(.addrWidth(24), .dataWidth(32), .bus("separate"), .Select("low")) ram_50 (
    .addr(Address_Bus[25:2]), .din(Data_Bus_In), .data(Data_Bus_Out), .str(Store), .sel(nand_50_out),
    .clk(CLK), .ld(Load), .clr(Clear));
  RAM #(.addrWidth(24), .dataWidth(32), .bus("separate"), .Select("low")) ram_51 (
    .addr(Address_Bus[25:2]), .din(Data_Bus_In), .data(Data_Bus_Out), .str(Store), .sel(nand_51_out),
    .clk(CLK), .ld(Load), .clr(Clear));
  RAM #(.addrWidth(24), .dataWidth(32), .bus("separate"), .Select("low")) ram_52 (
    .addr(Address_Bus[25:2]), .din(Data_Bus_In), .data(Data_Bus_Out), .str(Store), .sel(nand_52_out),
    .clk(CLK), .ld(Load), .clr(Clear));
  RAM #(.addrWidth(24), .dataWidth(32), .bus("separate"), .Select("low")) ram_53 (
    .addr(Address_Bus[25:2]), .din(Data_Bus_In), .data(Data_Bus_Out), .str(Store), .sel(nand_53_out),
    .clk(CLK), .ld(Load), .clr(Clear));
  RAM #(.addrWidth(24), .dataWidth(32), .bus("separate"), .Select("low")) ram_54 (
    .addr(Address_Bus[25:2]), .din(Data_Bus_In), .data(Data_Bus_Out), .str(Store), .sel(nand_54_out),
    .clk(CLK), .ld(Load), .clr(Clear));
  RAM #(.addrWidth(24), .dataWidth(32), .bus("separate"), .Select("low")) ram_55 (
    .addr(Address_Bus[25:2]), .din(Data_Bus_In), .data(Data_Bus_Out), .str(Store), .sel(nand_55_out),
    .clk(CLK), .ld(Load), .clr(Clear));
  RAM #(.addrWidth(24), .dataWidth(32), .bus("separate"), .Select("low")) ram_56 (
    .addr(Address_Bus[25:2]), .din(Data_Bus_In), .data(Data_Bus_Out), .str(Store), .sel(nand_56_out),
    .clk(CLK), .ld(Load), .clr(Clear));
  nand nand_57 (nand_57_out, decoder_2_out7, decoder_1_out0);
  nand nand_58 (nand_58_out, decoder_2_out7, decoder_1_out1);
  nand nand_59 (nand_59_out, decoder_2_out7, decoder_1_out2);
  nand nand_60 (nand_60_out, decoder_2_out7, decoder_1_out3);
  nand nand_61 (nand_61_out, decoder_2_out7, decoder_1_out4);
  nand nand_62 (nand_62_out, decoder_2_out7, decoder_1_out5);
  nand nand_63 (nand_63_out, decoder_2_out7, decoder_1_out6);
  nand nand_64 (nand_64_out, decoder_2_out7, decoder_1_out7);
  RAM #(.addrWidth(24), .dataWidth(32), .bus("separate"), .Select("low")) ram_57 (
    .addr(Address_Bus[25:2]), .din(Data_Bus_In), .data(Data_Bus_Out), .str(Store), .sel(nand_57_out),
    .clk(CLK), .ld(Load), .clr(Clear));
  RAM #(.addrWidth(24), .dataWidth(32), .bus("separate"), .Select("low")) ram_58 (
    .addr(Address_Bus[25:2]), .din(Data_Bus_In), .data(Data_Bus_Out), .str(Store), .sel(nand_58_out),
    .clk(CLK), .ld(Load), .clr(Clear));
  RAM #(.addrWidth(24), .dataWidth(32), .bus("separate"), .Select("low")) ram_59 (
    .addr(Address_Bus[25:2]), .din(Data_Bus_In), .data(Data_Bus_Out), .str(Store), .sel(nand_59_out),
    .clk(CLK), .ld(Load), .clr(Clear));
  RAM #(.addrWidth(24), .dataWidth(32), .bus("separate"), .Select("low")) ram_60 (
    .addr(Address_Bus[25:2]), .din(Data_Bus_In), .data(Data_Bus_Out), .str(Store), .sel(nand_60_out),
    .clk(CLK), .ld(Load), .clr(Clear));
  RAM #(.addrWidth(24), .dataWidth(32), .bus("separate"), .Select("low")) ram_61 (
    .addr(Address_Bus[25:2]), .din(Data_Bus_In), .data(Data_Bus_Out), .str(Store), .sel(nand_61_out),
    .clk(CLK), .ld(Load), .clr(Clear));
  RAM #(.addrWidth(24), .dataWidth(32), .bus("separate"), .Select("low")) ram_62 (
    .addr(Address_Bus[25:2]), .din(Data_Bus_In), .data(Data_Bus_Out), .str(Store), .sel(nand_62_out),
    .clk(CLK), .ld(Load), .clr(Clear));
  RAM #(.addrWidth(24), .dataWidth(32), .bus("separate"), .Select("low")) ram_63 (
    .addr(Address_Bus[25:2]), .din(Data_Bus_In), .data(Data_Bus_Out), .str(Store), .sel(nand_63_out),
    .clk(CLK), .ld(Load), .clr(Clear));
  RAM #(.addrWidth(24), .dataWidth(32), .bus("separate"), .Select("low")) ram_64 (
    .addr(Address_Bus[25:2]), .din(Data_Bus_In), .data(Data_Bus_Out), .str(Store), .sel(nand_64_out),
    .clk(CLK), .ld(Load), .clr(Clear));

  // Other names for the same wires on the sheet: Ad_TP[31:0] = Address_Bus; tunnel[23:0] = Address_Bus[25:2];
  //   Data_Bus_In_TP[31:0] = Data_Bus_In; DataOut[31:0] = Data_Bus_Out

  // Notes on the sheet:
  //   外部各接口定义与原RAM相同
  //   按照字节编址，但按照字对齐访问
endmodule

// ALU
module \算术逻辑运算单元ALU  (
  input  [31:0] X,
  input  [31:0] Y,
  input  [2:0] AluOP,
  output \结果是否为0 ,
  output [31:0] Result
);

  wire bitselector_1_out;
  wire [24:0] \运算指示 ;
  wire [31:0] adder_1_out, and_1_out, and_2_out, bit_extender_1_out, or_1_out, or_2_out, subtractor_1_out,
       undriven;

  // Probe on X
  // Probe on X
  // Probe on Y
  // Probe on Y
  // Probe on AluOP
  // Probe on Result
  // Probe on Result
  assign and_1_out = X & Y;  // AND_Gate and_1, 32 bits wide
  assign or_1_out = X | Y;  // OR_Gate or_1, 32 bits wide
  Adder #(.width(32)) adder_1 (.a(X), .b(Y), .out(adder_1_out));  // open: cin, cout
  assign and_2_out = X & ~Y;  // AND_Gate and_2, 32 bits wide
  assign or_2_out = X | ~Y;  // OR_Gate or_2, 32 bits wide
  Subtractor #(.width(32)) subtractor_1 (.a(X), .b(Y), .out(subtractor_1_out));  // open: bin, bout
  DotMatrix #(.inputtype("column"), .matrixcols(5), .matrixrows(5), .persist(0), .dotshape("square")) dotmatrix_1 (
    .col0(\运算指示 [24:20]), .col1(\运算指示 [19:15]), .col2(\运算指示 [14:10]), .col3(\运算指示 [9:5]), .col4(\运算指示 [4:0]));
  BitSelector #(.width(32), .group(1)) bitselector_1 (.in(subtractor_1_out), .out(bitselector_1_out), .sel({5{1'b1}}));
  assign bit_extender_1_out = {{31{1'b0}}, bitselector_1_out};  // Bit_Extender bit_extender_1
  Multiplexer #(.select(3), .width(32), .disabled("Z"), .enable("false")) multiplexer_1 (
    .in0(and_1_out), .in1(or_1_out), .in2(adder_1_out), .in3(undriven), .in4(and_2_out), .in5(or_2_out),
    .in6(subtractor_1_out), .in7(bit_extender_1_out), .out(Result), .sel(AluOP));
  Comparator #(.width(32), .mode("twosComplement")) comparator_1 (
    .a(Result), .b({32{1'b0}}), .eq(\结果是否为0 ));  // open: gt, lt
  Multiplexer #(.select(3), .width(25), .disabled("Z"), .enable("false")) multiplexer_2 (
    .in0(25'h124081), .in1(25'h1020490), .in2(25'h427c84), .in3({25{1'b0}}), .in4(25'h124091),
    .in5(25'h1020490), .in6(25'h421084), .in7(25'h402811), .out(\运算指示 ), .sel(AluOP));

  // Other names for the same wires on the sheet: S[2:0] = AluOP; Zero = \结果是否为0 

  // Notes on the sheet:
  //   Y: pull=down
  //   AluOP: pull=down
  //   X: pull=down
  //   不要改变此引脚区域内容，也不要改变ALU封装形式
  //   请在下方利用上方输入输出引脚的隧道信号构建ALU电路，ctrl+d复制选择部件
  //   输入引脚
  //   探测区域
  //   输出引脚
  //   功能说明：
  //   000：X AND Y      100：X AND Y'
  //   001：X OR Y        101：X OR Y'  
  //   010：X + Y           110：X - Y  
  //   011：未使用         111：SLT  
endmodule

module \ALU自动测试  (
  output [7:0] TEST_num
);

  wire ADD, AND, and_1_out, AND_prime, CLK, comparator_2_eq, HALT, Halt_t, multiplexer_1_out, nHalt, NotEQ,
       OR, OR_prime, priority_encoder_1_gs, Rok, SLT, SUB, X___Y, X___Y_t, X_AND_Y, X_AND_Y_prime, X_OR_Y,
       X_OR_Y_prime, X_Y, xnor_1_out, Zero, Zero_Standard, \悬空检测 ;
  wire [2:0] ALUOP;
  wire [3:0] \个位 , \十位 , \百位 ;
  wire [7:0] adder_1_out, \单项评分_1_总条数 , \单项评分_1_扣分 , \单项评分_1_正确条数 , \单项评分_2_总条数 , \单项评分_2_扣分 , \单项评分_2_正确条数 ,
       \单项评分_3_总条数 , \单项评分_3_扣分 , \单项评分_3_正确条数 , \单项评分_4_总条数 , \单项评分_4_扣分 , \单项评分_4_正确条数 , \单项评分_5_总条数 ,
       \单项评分_5_扣分 , \单项评分_5_正确条数 , \单项评分_6_总条数 , \单项评分_6_扣分 , \单项评分_6_正确条数 , \单项评分_7_总条数 , \单项评分_7_扣分 ,
       \单项评分_7_正确条数 , \单项评分_8_扣分 , \总项评分_1_总分 ;
  wire [9:0] counter_1_q;
  wire [31:0] bit_extender_1_out, R, R_Standard, X, Y;

  Register #(.width(8), .trigger("rising"), .Select("low")) register_1 (
    .D(adder_1_out), .en(nHalt), .Q(TEST_num), .clk(CLK));  // open: clr
  Clock #(.highDuration(1), .lowDuration(1)) clock_1 (.out(CLK));
  \单项评分  \u_单项评分_1  (
    .ALUOP(AND), .\扣分 (\单项评分_1_扣分 ), .\正确条数 (\单项评分_1_正确条数 ), .Rok(Rok), .nHalt(nHalt), .Right(X_AND_Y),
    .CLK(CLK), .\总条数 (\单项评分_1_总条数 ), .NotEQ(NotEQ));
  // Probe on \单项评分_1_总条数 
  // Probe on \单项评分_1_正确条数 
  // Probe on \单项评分_1_扣分 
  Adder #(.width(8)) adder_1 (.a(8'h1), .b(TEST_num), .out(adder_1_out));  // open: cin, cout
  not not_1 (nHalt, Halt_t);
  Comparator #(.width(3), .mode("twosComplement")) comparator_1 (.a(ALUOP), .b(3'b011), .eq(Halt_t));  // open: gt, lt
  Counter #(.width(10), .max('h3ff), .ongoal("wrap"), .trigger("rising"), .behavior("old")) counter_1 (
    .count(NotEQ), .Q(counter_1_q), .clk(CLK), .clr(Halt_t));  // open: load, D, carry, preset
  and and_1 (and_1_out, ~Halt_t, NotEQ);  // AND_Gate
  \单项评分  \u_单项评分_2  (
    .ALUOP(OR), .\扣分 (\单项评分_2_扣分 ), .\正确条数 (\单项评分_2_正确条数 ), .Rok(Rok), .nHalt(nHalt), .Right(X_OR_Y),
    .CLK(CLK), .\总条数 (\单项评分_2_总条数 ), .NotEQ(NotEQ));
  // Probe on \单项评分_2_总条数 
  // Probe on \单项评分_2_正确条数 
  // Probe on \单项评分_2_扣分 
  \总项评分  \u_总项评分_1  (
    .in_1(\单项评分_1_扣分 ), .in_2(\单项评分_2_扣分 ), .in_3(\单项评分_3_扣分 ), .in_4(\单项评分_4_扣分 ), .in_5(\单项评分_5_扣分 ),
    .in_6(\单项评分_6_扣分 ), .in_8(\单项评分_7_扣分 ), .in_9(\单项评分_8_扣分 ), .\总分 (\总项评分_1_总分 ), .\百位 (\百位 ), .\十位 (\十位 ),
    .\个位 (\个位 ), .\Zero悬空扣分 (\悬空检测 ));
  trace trace_1 (.in_1(TEST_num), .X(X), .Y(Y), .AluOP(ALUOP), .R(R_Standard), .Zero(Zero_Standard));
  \单项评分  \u_单项评分_3  (
    .ALUOP(ADD), .\扣分 (\单项评分_3_扣分 ), .\正确条数 (\单项评分_3_正确条数 ), .Rok(Rok), .nHalt(nHalt), .Right(X___Y),
    .CLK(CLK), .\总条数 (\单项评分_3_总条数 ), .NotEQ(NotEQ));
  // Probe on \单项评分_3_总条数 
  // Probe on \单项评分_3_正确条数 
  // Probe on \单项评分_3_扣分 
  RAM #(.addrWidth(10), .dataWidth(32), .bus("separate"), .Select("low")) ram_1 (
    .addr(counter_1_q), .din(X), .str(and_1_out), .clk(CLK));  // open: data, sel, ld, clr
  \单项评分  \u_单项评分_4  (
    .ALUOP(AND_prime), .\扣分 (\单项评分_4_扣分 ), .\正确条数 (\单项评分_4_正确条数 ), .Rok(Rok), .nHalt(nHalt),
    .Right(X_AND_Y_prime), .CLK(CLK), .\总条数 (\单项评分_4_总条数 ), .NotEQ(NotEQ));
  // Probe on \单项评分_4_总条数 
  // Probe on \单项评分_4_正确条数 
  // Probe on \单项评分_4_扣分 
  \单项评分  \u_单项评分_5  (
    .ALUOP(OR_prime), .\扣分 (\单项评分_5_扣分 ), .\正确条数 (\单项评分_5_正确条数 ), .Rok(Rok), .nHalt(nHalt),
    .Right(X_OR_Y_prime), .CLK(CLK), .\总条数 (\单项评分_5_总条数 ), .NotEQ(NotEQ));
  // Probe on \单项评分_5_总条数 
  // Probe on \单项评分_5_正确条数 
  // Probe on \单项评分_5_扣分 
  // Probe on \总项评分_1_总分 
  \算术逻辑运算单元ALU  \u_算术逻辑运算单元alu_1  (.AluOP(ALUOP), .X(X), .Result(R), .Y(Y), .\结果是否为0 (Zero));
  RAM #(.addrWidth(10), .dataWidth(32), .bus("separate"), .Select("low")) ram_2 (
    .addr(counter_1_q), .din(Y), .str(and_1_out), .clk(CLK));  // open: data, sel, ld, clr
  assign bit_extender_1_out = {{29{1'b0}}, ALUOP};  // Bit_Extender bit_extender_1
  \单项评分  \u_单项评分_6  (
    .ALUOP(SUB), .\扣分 (\单项评分_6_扣分 ), .\正确条数 (\单项评分_6_正确条数 ), .Rok(Rok), .nHalt(nHalt), .Right(X___Y_t),
    .CLK(CLK), .\总条数 (\单项评分_6_总条数 ), .NotEQ(NotEQ));
  // Probe on \单项评分_7_总条数 
  // Probe on \单项评分_6_总条数 
  // Probe on \单项评分_6_正确条数 
  // Probe on \单项评分_6_扣分 
  \单项评分  \u_单项评分_7  (
    .ALUOP(SLT), .\扣分 (\单项评分_7_扣分 ), .\正确条数 (\单项评分_7_正确条数 ), .Rok(Rok), .nHalt(nHalt), .Right(X_Y),
    .CLK(CLK), .\总条数 (\单项评分_7_总条数 ), .NotEQ(NotEQ));
  // Probe on \单项评分_7_正确条数 
  // Probe on \单项评分_7_扣分 
  // Probe on ALUOP
  \单项评分  \u_单项评分_8  (
    .ALUOP(1'b0), .\扣分 (\单项评分_8_扣分 ), .Rok(Rok), .nHalt(nHalt), .CLK(CLK), .NotEQ(NotEQ));  // open: 正确条数, Right, 总条数
  RAM #(.addrWidth(10), .dataWidth(32), .bus("separate"), .Select("low")) ram_3 (
    .addr(counter_1_q), .din(bit_extender_1_out), .str(and_1_out), .clk(CLK));  // open: data, sel, ld, clr
  Decoder #(.select(3), .tristate("false"), .disabled("Z"), .enable("false")) decoder_1 (
    .out0(AND), .out1(OR), .out2(ADD), .out3(HALT), .out4(AND_prime), .out5(OR_prime), .out6(SUB),
    .out7(SLT), .sel(ALUOP));
  Multiplexer #(.select(1), .width(1), .disabled("Z"), .enable("false")) multiplexer_1 (
    .in0(1'b1), .in1(1'b1), .out(multiplexer_1_out), .sel(Zero));
  xnor xnor_1 (xnor_1_out, Zero_Standard, Zero);
  Comparator #(.width(32), .mode("twosComplement")) comparator_2 (
    .a(R_Standard), .b(R), .eq(comparator_2_eq));  // open: gt, lt
  LED #(.active("false")) led_1 (.in(X_AND_Y));
  LED #(.active("false")) led_2 (.in(X_OR_Y));
  LED #(.active("false")) led_3 (.in(X___Y));
  LED #(.active("false")) led_4 (.in(X_AND_Y_prime));
  LED #(.active("false")) led_5 (.in(X_OR_Y_prime));
  LED #(.active("false")) led_6 (.in(X___Y_t));
  LED #(.active("false")) led_7 (.in(X_Y));
  LED #(.active("true")) led_8 (.in(NotEQ));
  Priority_Encoder #(.select(1), .disabled("Z")) priority_encoder_1 (
    .in0(multiplexer_1_out), .in1(multiplexer_1_out), .gs(priority_encoder_1_gs));  // open: out, en_out, en_in
  not not_2 (\悬空检测 , priority_encoder_1_gs);
  nand nand_1 (NotEQ, xnor_1_out, Rok);
  Priority_Encoder #(.select(1), .disabled("Z")) priority_encoder_2 (
    .in0(comparator_2_eq), .in1(comparator_2_eq), .gs(Rok));  // open: out, en_out, en_in
  Hex_Digit_Display hex_digit_display_1 (.value(\百位 ));  // open: dp
  Hex_Digit_Display hex_digit_display_2 (.value(\十位 ));  // open: dp
  Hex_Digit_Display hex_digit_display_3 (.value(\个位 ));  // open: dp

  // Notes on the sheet:
  //   X 错误记录
  //   Y 错误记录
  //   ALUOP 错误记录
  //   运算故障指示
  //   红色异常
  //   成绩
endmodule

module trace (
  input  [7:0] in_1,
  output [31:0] X,
  output [31:0] Y,
  output [2:0] AluOP,
  output [31:0] R,
  output Zero
);

  ROM #(.addrWidth(8), .dataWidth(32), .Select("high")) rom_1 (.addr(in_1), .data(X));
  ROM #(.addrWidth(8), .dataWidth(32), .Select("high")) rom_2 (.addr(in_1), .data(Y));
  ROM #(.addrWidth(8), .dataWidth(3), .Select("high")) rom_3 (.addr(in_1), .data(AluOP));
  ROM #(.addrWidth(8), .dataWidth(32), .Select("high")) rom_4 (.addr(in_1), .data(R));
  ROM #(.addrWidth(8), .dataWidth(1), .Select("high")) rom_5 (.addr(in_1), .data(Zero));

  // Notes on the sheet:
  //   X trace
  //   contents of rom_1 (hex, n*v repeats v):
  //   1 1 1 0 11111111 0 0 0 10b67f2
  //   Y trace
  //   contents of rom_2 (hex, n*v repeats v):
  //   1 0 1 4*0 1 2f5a0df4
  //   ALU OP Trace
  //   contents of rom_3 (hex, n*v repeats v):
  //   0 1 2 0 4 5 6 7 2
  //   Result
  //   contents of rom_4 (hex, n*v repeats v):
  //   1 1 2 0 11111111 ffffffff 0 1 306575e6
  //   Zero Flag
  //   contents of rom_5 (hex, n*v repeats v):
  //   0 0 0 1 0 0 1 0 0 247*1
endmodule

module \单项评分  (
  input  ALUOP,
  input  NotEQ,
  input  Rok,
  input  nHalt,
  input  CLK,
  output [7:0] \扣分 ,
  output [7:0] \正确条数 ,
  output Right,
  output [7:0] \总条数 
);

  wire and_1_out, and_2_out, and_3_out, and_4_out, comparator_1_eq, not_1_out, not_2_out, not_3_out,
       undriven, undriven_2, undriven_3, undriven_4;
  wire [7:0] counter_1_q, counter_2_q, multiplexer_1_out;

  not not_1 (not_1_out, NotEQ);
  and and_1 (and_1_out, undriven, undriven_2, undriven_3);
  and and_2 (and_2_out, undriven, undriven_3);
  and and_3 (and_3_out, ALUOP, not_1_out, Rok, nHalt);
  and and_4 (and_4_out, ALUOP, nHalt);
  Counter #(.width(8), .max('hff), .ongoal("wrap"), .trigger("rising"), .behavior("new")) counter_1 (
    .Q(counter_1_q), .clk(undriven_4), .down(and_1_out));  // open: load, D, count, carry, clr, preset
  Counter #(.width(8), .max('hff), .ongoal("wrap"), .trigger("rising"), .behavior("new")) counter_2 (
    .Q(counter_2_q), .down(and_2_out));  // open: load, D, count, carry, clk, clr, preset
  Counter #(.width(8), .max('hff), .ongoal("wrap"), .trigger("rising"), .behavior("old")) counter_3 (
    .count(and_3_out), .Q(\正确条数 ), .clk(CLK));  // open: load, D, carry, clr, preset
  Counter #(.width(8), .max('hff), .ongoal("wrap"), .trigger("rising"), .behavior("old")) counter_4 (
    .count(and_4_out), .Q(\总条数 ), .clk(CLK));  // open: load, D, carry, clr, preset
  Comparator #(.width(8), .mode("twosComplement")) comparator_1 (
    .a(counter_1_q), .b(counter_2_q), .eq(comparator_1_eq));  // open: gt, lt
  Comparator #(.width(8), .mode("twosComplement")) comparator_2 (.a(\正确条数 ), .b(\总条数 ), .eq(Right));  // open: gt, lt
  Multiplexer #(.select(1), .width(8), .disabled("Z"), .enable("false")) multiplexer_1 (
    .in0({8{1'b0}}), .in1(8'h5), .out(multiplexer_1_out), .sel(not_2_out));
  not not_2 (not_2_out, comparator_1_eq);
  not not_3 (not_3_out, Right);
  Multiplexer #(.select(1), .width(8), .disabled("Z"), .enable("false")) multiplexer_2 (
    .in0({8{1'b0}}), .in1(8'h5), .out(\扣分 ), .sel(not_3_out));

  // Notes on the sheet:
  //   ALUOP
  //   Rok
  //   ~Halt
  //   CLK
  //   Duplicated
  //   总条数
  //   正确条数
  //   扣分
  //   Right？
endmodule

module \总项评分  (
  input  [7:0] in_1,
  input  [7:0] in_2,
  input  [7:0] in_3,
  input  [7:0] in_4,
  input  [7:0] in_5,
  input  [7:0] in_6,
  input  \Zero悬空扣分 ,
  input  [7:0] in_8,
  input  [7:0] in_9,
  output [7:0] \总分 ,
  output [3:0] \百位 ,
  output [3:0] \十位 ,
  output [3:0] \个位 
);

  wire [7:0] adder_1_out, adder_2_out, adder_3_out, adder_4_out, adder_5_out, adder_6_out, adder_7_out,
       divider_1_out, subtractor_1_out, subtractor_2_out;
  wire [7:4] divider_1_rem, divider_2_out, divider_2_rem;

  Adder #(.width(8)) adder_1 (.a(in_1), .b(in_2), .out(adder_1_out));  // open: cin, cout
  Adder #(.width(8)) adder_2 (.a(in_3), .b(in_4), .out(adder_2_out));  // open: cin, cout
  Adder #(.width(8)) adder_3 (.a(in_5), .b(in_6), .out(adder_3_out));  // open: cin, cout
  Adder #(.width(8)) adder_4 (.a(in_8), .b(in_9), .out(adder_4_out));  // open: cin, cout
  Adder #(.width(8)) adder_5 (.a(adder_1_out), .b(adder_2_out), .out(adder_5_out));  // open: cin, cout
  Adder #(.width(8)) adder_6 (.a(adder_3_out), .b(adder_4_out), .out(adder_6_out));  // open: cin, cout
  Adder #(.width(8)) adder_7 (.a(adder_5_out), .b(adder_6_out), .out(adder_7_out));  // open: cin, cout
  Subtractor #(.width(8)) subtractor_1 (.a(8'h64), .b(adder_7_out), .out(subtractor_1_out));  // open: bin, bout
  Subtractor #(.width(8)) subtractor_2 (.a(subtractor_1_out), .b(8'h5), .out(subtractor_2_out));  // open: bin, bout
  Multiplexer #(.select(1), .width(8), .disabled("Z"), .enable("false")) multiplexer_1 (
    .in0(subtractor_1_out), .in1(subtractor_2_out), .out(\总分 ), .sel(\Zero悬空扣分 ));
  Divider #(.width(8)) divider_1 (.a(\总分 ), .b(8'ha), .out(divider_1_out), .rem({divider_1_rem, \个位 }));  // open: upper
  Divider #(.width(8)) divider_2 (
    .a(divider_1_out), .b(8'ha), .out({divider_2_out, \百位 }), .rem({divider_2_rem, \十位 }));  // open: upper
endmodule

module ControlUnit (
  input  [5:0] Op,
  input  [5:0] Funct,
  output MemtoReg,
  output MemWrite,
  output Branch,
  output ALUSrc,
  output RegDst,
  output [2:0] ALUControl,
  output RegWrite,
  output syscall,
  output Jump
);

  wire and_1_out, and_2_out, and_7_out, and_8_out, and_9_out, and_10_out, not_1_out, not_2_out, not_3_out,
       not_4_out, not_5_out, not_6_out, not_7_out;
  wire [1:1] ALUOp;

  not not_1 (not_1_out, Op[2]);
  not not_2 (not_2_out, Op[1]);
  not not_3 (not_3_out, Op[3]);
  not not_4 (not_4_out, Op[3]);
  not not_5 (not_5_out, Op[1]);
  and and_1 (and_1_out, not_1_out, not_2_out);
  and and_2 (and_2_out, not_3_out, Op[5]);
  and and_3 (ALUOp[1], ~Op[1], ~Op[3], ~Op[2]);  // AND_Gate
  not not_6 (not_6_out, Op[0]);
  and and_4 (MemWrite, Op[3], Op[5]);
  or or_1 (ALUSrc, Op[1], Op[3]);
  and and_5 (RegDst, not_4_out, not_5_out);
  or or_2 (RegWrite, and_1_out, and_2_out);
  and and_6 (Jump, Op[1], not_6_out);
  not not_7 (not_7_out, ALUOp[1]);
  and and_7 (and_7_out, ALUOp[1], Funct[0]);
  and and_8 (and_8_out, ALUOp[1], Funct[3]);
  or or_3 (ALUControl[1], ~ALUOp[1], ~Funct[2]);  // OR_Gate
  and and_9 (and_9_out, Op[2], not_7_out);
  and and_10 (and_10_out, ALUOp[1], Funct[1]);
  or or_4 (ALUControl[0], and_7_out, and_8_out);
  or or_5 (ALUControl[2], and_9_out, and_10_out);
  Comparator #(.width(6), .mode("twosComplement")) comparator_1 (
    .a(Funct), .b(6'b001100), .eq(syscall));  // open: gt, lt

  assign Branch = Op[2];
  assign MemtoReg = Op[1];

  // Other names for the same wires on the sheet: ALUOp[0] = Op[2]

  // Notes on the sheet:
  //   b
  //   a
endmodule

module test (
  input  s5,
  input  s4,
  input  s3,
  input  s2,
  input  s1,
  input  s0,
  output regw,
  output regd,
  output alus,
  output bra,
  output memw,
  output memto,
  output aluop1,
  output aluop0,
  output jump
);

  wire and_2_out, and_3_out, not_1_out, not_2_out, not_3_out, not_4_out, not_5_out, not_6_out, not_7_out,
       not_8_out, not_9_out;

  not not_1 (not_1_out, s2);
  not not_2 (not_2_out, s1);
  not not_3 (not_3_out, s3);
  not not_4 (not_4_out, s3);
  not not_5 (not_5_out, s1);
  or or_1 (alus, s1, s3);
  and and_1 (memw, s5, s3);
  not not_6 (not_6_out, s3);
  not not_7 (not_7_out, s2);
  not not_8 (not_8_out, s1);
  not not_9 (not_9_out, s0);
  and and_2 (and_2_out, not_1_out, not_2_out);
  and and_3 (and_3_out, s5, not_3_out);
  and and_4 (regd, not_4_out, not_5_out);
  and and_5 (aluop1, not_6_out, not_7_out, not_8_out);
  and and_6 (jump, s1, not_9_out);
  or or_2 (regw, and_2_out, and_3_out);

  assign aluop0 = s2;
  assign bra = s2;
  assign memto = s1;
endmodule

module \红绿灯控制电路  (
  input  S1,
  input  S0,
  output R1,
  output G1,
  output Y1,
  output R2,
  output G2,
  output Y2
);

  wire not_1_out, not_2_out, not_3_out, not_5_out;

  not not_1 (not_1_out, S1);
  not not_2 (not_2_out, S0);
  not not_3 (not_3_out, S1);
  not not_4 (R2, S1);
  not not_5 (not_5_out, S0);
  and and_1 (Y2, S1, S0);
  and and_2 (G1, not_1_out, not_2_out);
  and and_3 (Y1, not_3_out, S0);
  and and_4 (G2, S1, not_5_out);

  assign R1 = S1;
endmodule

module _7_segment (
  input  a,
  input  b,
  input  c,
  input  d,
  output y1,
  output y2,
  output y3,
  output y4,
  output y5,
  output y6,
  output y7
);

  wire and_1_out, and_2_out, and_3_out, and_4_out, and_5_out, and_6_out, and_7_out, and_8_out, and_9_out,
       and_10_out, and_11_out, and_12_out, and_13_out, and_14_out, and_15_out, and_16_out, not_1_out,
       not_2_out, not_3_out, not_4_out, not_5_out, not_6_out, not_7_out, not_8_out, not_9_out, not_10_out,
       not_11_out, not_12_out, not_13_out, not_14_out, not_15_out, not_16_out, not_17_out, not_18_out,
       not_19_out, not_20_out, not_21_out;

  not not_1 (not_1_out, b);
  and and_1 (and_1_out, not_1_out, not_2_out);
  not not_2 (not_2_out, d);
  and and_2 (and_2_out, b, d);
  not not_3 (not_3_out, b);
  not not_4 (not_4_out, c);
  and and_3 (and_3_out, not_4_out, not_5_out);
  not not_5 (not_5_out, d);
  and and_4 (and_4_out, c, d);
  not not_6 (not_6_out, c);
  or or_1 (y3, not_6_out, d, b);
  not not_7 (not_7_out, b);
  and and_5 (and_5_out, not_7_out, not_8_out);
  not not_8 (not_8_out, d);
  not not_9 (not_9_out, b);
  and and_6 (and_6_out, not_9_out, c);
  and and_7 (and_7_out, c, not_10_out);
  not not_10 (not_10_out, d);
  not not_11 (not_11_out, c);
  and and_8 (and_8_out, b, not_11_out, d);
  not not_12 (not_12_out, b);
  and and_9 (and_9_out, not_12_out, not_13_out);
  not not_13 (not_13_out, d);
  and and_10 (and_10_out, c, not_14_out);
  not not_14 (not_14_out, d);
  not not_15 (not_15_out, c);
  and and_11 (and_11_out, not_15_out, not_16_out);
  not not_16 (not_16_out, d);
  and and_12 (and_12_out, b, not_17_out);
  not not_17 (not_17_out, c);
  and and_13 (and_13_out, b, not_18_out);
  not not_18 (not_18_out, d);
  not not_19 (not_19_out, b);
  and and_14 (and_14_out, not_19_out, c);
  and and_15 (and_15_out, b, not_20_out);
  not not_20 (not_20_out, c);
  and and_16 (and_16_out, b, not_21_out);
  not not_21 (not_21_out, d);
  or or_2 (y1, and_1_out, c, and_2_out, a);
  or or_3 (y2, not_3_out, and_3_out, and_4_out);
  or or_4 (y4, and_5_out, and_6_out, and_7_out, and_8_out, a);
  or or_5 (y5, and_9_out, and_10_out);
  or or_6 (y6, and_11_out, and_12_out, and_13_out, a);
  or or_7 (y7, and_14_out, and_15_out, and_16_out, a);
endmodule

module FSM_new (
  input  Ta,
  input  Tb,
  output S1,
  output S0
);

  wire and_1_out, and_2_out, clock_1_out;
  wire [1:0] xor_1_out;

  and and_1 (and_1_out, ~S1, ~S0, ~Ta);  // AND_Gate
  and and_2 (and_2_out, S1, ~S0, ~Tb);  // AND_Gate
  xor xor_1 (xor_1_out[0], S1, S0);
  or or_1 (xor_1_out[1], and_1_out, and_2_out);
  Register #(.width(2), .trigger("rising"), .Select("high")) \u_寄存器_时序逻辑  (
    .D(xor_1_out), .Q({S0, S1}), .clk(clock_1_out), .cs(1'b1));  // open: en, clr, preset
  Clock #(.highDuration(5), .lowDuration(5)) clock_1 (.out(clock_1_out));
endmodule

module adder_1 (
  input  x,
  input  y,
  input  cin,
  output s,
  output cout
);

  wire and_1_out, and_2_out, and_3_out, and_4_out, and_5_out, and_6_out, and_7_out, and_8_out, and_9_out,
       and_10_out, and_11_out, not_1_out, not_2_out, not_3_out, not_4_out, not_5_out, not_6_out, or_1_out,
       or_3_out, or_4_out;

  not not_1 (not_1_out, x);
  not not_2 (not_2_out, y);
  not not_3 (not_3_out, x);
  not not_4 (not_4_out, y);
  and and_1 (and_1_out, y, cin);
  and and_2 (and_2_out, x, cin);
  and and_3 (and_3_out, not_1_out, not_2_out);
  and and_4 (and_4_out, not_3_out, y);
  not not_5 (not_5_out, cin);
  and and_5 (and_5_out, x, not_4_out);
  not not_6 (not_6_out, cin);
  and and_6 (and_6_out, x, y);
  or or_1 (or_1_out, and_1_out, and_2_out);
  and and_7 (and_7_out, x, y);
  and and_8 (and_8_out, and_3_out, cin);
  and and_9 (and_9_out, and_4_out, not_5_out);
  and and_10 (and_10_out, and_5_out, not_6_out);
  and and_11 (and_11_out, and_6_out, cin);
  or or_2 (cout, or_1_out, and_7_out);
  or or_3 (or_3_out, and_8_out, and_9_out);
  or or_4 (or_4_out, and_10_out, and_11_out);
  or or_5 (s, or_3_out, or_4_out);
endmodule

module adder_4 (
  input  x0,
  input  x1,
  input  x2,
  input  x3,
  input  initial_cin,
  input  y0,
  input  y1,
  input  y2,
  input  y3,
  output z0,
  output z1,
  output z2,
  output z3,
  output z4
);

  wire adder_1_1_cout, adder_1_2_cout, adder_1_3_cout;

  adder_1 adder_1_1 (.x(x0), .y(y0), .cin(initial_cin), .s(z0), .cout(adder_1_1_cout));
  adder_1 adder_1_2 (.x(x1), .y(y1), .cin(adder_1_1_cout), .s(z1), .cout(adder_1_2_cout));
  adder_1 adder_1_3 (.x(x2), .y(y2), .cin(adder_1_2_cout), .s(z2), .cout(adder_1_3_cout));
  adder_1 adder_1_4 (.x(x3), .y(y3), .cin(adder_1_3_cout), .s(z3), .cout(z4));
endmodule

module _8421BCD (
  input  x4,
  input  x3,
  input  x2,
  input  x1,
  input  x0,
  output y7,
  output y6,
  output y5,
  output y4,
  output y3,
  output y2,
  output y1,
  output y0
);

  wire and_1_out, and_2_out, and_3_out, and_4_out, and_5_out, and_6_out, and_7_out, and_8_out, and_9_out,
       and_10_out, not_1_out, not_2_out, not_3_out, not_4_out, not_5_out, not_6_out, not_7_out, not_8_out;

  and and_1 (and_1_out, x3, x1);
  and and_2 (and_2_out, x3, x2);
  not not_1 (not_1_out, x2);
  not not_2 (not_2_out, x1);
  not not_3 (not_3_out, x3);
  not not_4 (not_4_out, x1);
  not not_5 (not_5_out, x4);
  not not_6 (not_6_out, x3);
  not not_7 (not_7_out, x1);
  not not_8 (not_8_out, x1);
  or or_1 (y4, and_1_out, and_2_out, x4);
  and and_3 (and_3_out, x3, not_1_out, not_2_out);
  and and_4 (and_4_out, x4, x1);
  and and_5 (and_5_out, not_3_out, x2);
  and and_6 (and_6_out, x2, x1);
  and and_7 (and_7_out, x4, not_4_out);
  and and_8 (and_8_out, not_5_out, not_6_out, x1);
  and and_9 (and_9_out, x3, x2, not_7_out);
  and and_10 (and_10_out, x4, not_8_out);
  or or_2 (y3, and_3_out, and_4_out);
  or or_3 (y2, and_5_out, and_6_out, and_7_out);
  or or_4 (y1, and_8_out, and_9_out, and_10_out);

  assign y0 = x0;
  assign y5 = 1'b0;
  assign y6 = 1'b0;
  assign y7 = 1'b0;
endmodule

module _4_10decoder (
  input  x0,
  input  x1,
  input  x2,
  input  x4,
  output y0,
  output y1,
  output y2,
  output y3,
  output y4,
  output y5,
  output y6,
  output y7,
  output y8,
  output y9
);

  wire not_1_out, not_2_out, not_3_out, not_4_out, not_5_out, not_6_out, not_7_out, not_8_out, not_9_out,
       not_10_out, not_11_out, not_12_out, not_13_out, not_14_out, not_15_out;

  not not_1 (not_1_out, x0);
  not not_2 (not_2_out, x1);
  not not_3 (not_3_out, x2);
  not not_4 (not_4_out, x4);
  not not_5 (not_5_out, x1);
  not not_6 (not_6_out, x2);
  not not_7 (not_7_out, x4);
  not not_8 (not_8_out, x0);
  and and_1 (y2, not_8_out, x1, not_9_out);
  not not_9 (not_9_out, x2);
  and and_2 (y3, x0, x1, not_10_out);
  not not_10 (not_10_out, x2);
  not not_11 (not_11_out, x0);
  and and_3 (y4, not_11_out, not_12_out, x2);
  not not_12 (not_12_out, x1);
  and and_4 (y5, x0, not_13_out, x2);
  not not_13 (not_13_out, x1);
  not not_14 (not_14_out, x0);
  and and_5 (y6, not_14_out, x1, x2);
  and and_6 (y7, x0, x1, x2);
  not not_15 (not_15_out, x0);
  and and_7 (y8, not_15_out, x4);
  and and_8 (y9, x0, x4);
  and and_9 (y0, not_1_out, not_2_out, not_3_out, not_4_out);
  and and_10 (y1, x0, not_5_out, not_6_out, not_7_out);
endmodule
